// Digital circuit Instructions rom.dig as structural Verilog
module Instructions_rom (
  input  [31:0] addr,
  output [31:0] instr
);

  ROM #(.AddrBits(10), .isProgramMemory("true"), .Bits(32)) Instructions_rom (.A(addr[11:2]), .sel(1'b1), .D(instr));

  // Notes on the sheet:
  //   contents of Instructions_rom (hex, n*v repeats v):
  //   67800093,123450b7,fff00113,abcde137,1101b3,40110233,1172b3,116333
  //   ,1143b3,111433,1154b3,40115533,abcde137,1125b3,113633,67810693
  //   ,67817713,67816793,67814813,111893,215913,40315993,412a13,513a93
  //   ,fa708ae3,fa8118e3,fa91d6e3,faa274e3,fab2c2e3,fab360e3,1000a3
  //   ,101123,102223,500083,704083,601083,405083,2083,f7dff06f,fffff017,67
endmodule
