// Digital circuit control unit.dig as structural Verilog
module control_unit (
  input  [4:0] instr,
  output [1:0] PC_mux,
  output RF_w,
  output A_mux,
  output [1:0] B_mux,
  output ALU_mux,
  output RAM_w,
  output [1:0] RF_mux,
  output SUM_mux
);

  wire and_1_out, and_2_out, and_3_out, and_4_out, and_5_out, and_7_out, and_8_out, and_9_out, not_2_out,
       not_4_out, not_5_out;

  not not_1 (SUM_mux, instr[0]);
  not not_2 (not_2_out, instr[1]);
  not not_3 (RF_mux[1], instr[2]);
  not not_4 (not_4_out, instr[3]);
  not not_5 (not_5_out, instr[4]);
  and and_1 (and_1_out, SUM_mux, instr[4]);
  and and_2 (and_2_out, instr[0], instr[2]);
  and and_3 (and_3_out, RF_mux[1], instr[3], not_5_out);
  and and_4 (and_4_out, instr[0], instr[2]);
  and and_5 (and_5_out, RF_mux[1], not_5_out);
  and and_6 (RAM_w, RF_mux[1], instr[3], not_5_out);
  and and_7 (and_7_out, instr[0], not_4_out);
  and and_8 (and_8_out, SUM_mux, instr[2]);
  and and_9 (and_9_out, instr[0], RF_mux[1]);
  or or_1 (PC_mux[1], SUM_mux, instr[2]);
  or or_2 (PC_mux[0], and_1_out, instr[1]);
  or or_3 (RF_w, instr[0], instr[2], not_4_out);
  or or_4 (A_mux, SUM_mux, RF_mux[1]);
  or or_5 (B_mux[1], and_2_out, and_3_out);
  or or_6 (B_mux[0], instr[0], not_4_out);
  or or_7 (ALU_mux, and_4_out, and_5_out);
  or or_8 (RF_mux[0], and_7_out, and_8_out, and_9_out);
endmodule

/* Test case:
instr  PC_mux RF_w A_mux B_mux ALU_mux RAM_w RF_mux  SUM_mux

#op-imm [00-100-11] : 10-1-1-01-0-0-01-X
4      2      1    1     1     0       0     1       x
#op     [01-100-11] : 10-1-1-00-0-0-01-X
12     2      1    1     0     0       0     1       x
#store  [01-000-11] : 10-0-1-10-1-1-XX-X
8      2      0    1     2     1       1     x       x
#load   [00-000-11] : 10-1-1-01-1-0-10-X
0      2      1    1     1     1       0     2       x
#branch [11-000-11] : 11-0-1-00-0-0-XX-1
24     3      0    1     0     0       0     x       1
#lui    [01-101-11] : 10-1-X-XX-X-0-00-X
13     2      1    x     x     x       0     0       x
#auipc  [00-101-11] : 10-1-0-11-1-0-01-X
5      2      1    0     3     1       0     1       x
#jal    [11-011-11] : 01-1-X-XX-X-0-11-0
27     1      1    x     x     x       0     3       0
#jalr   [11-001-11] : 00-1-1-01-0-0-11-X
25     0      1    1     1     0       0     3       x
*/
