// Digital circuit cpu.dig as structural Verilog
module cpu (
  input  clk
);

  wire _5, _7, _20, _30, _31, A_mux, ALU_mux, arethmetic_and_logic_unit_1_bcond, RAM_w, RF_w, SUM_mux;
  wire [1:0] B_mux, PC_mux, RF_mux;
  wire [2:0] funct3_14_12, multiplexer_6_out;
  wire [3:0] _11_8;
  wire [6:0] opcode_6_0;
  wire [7:3] imm_19_12;
  wire [8:0] _30_21;
  wire [31:0] adder_2_p1, adder_2_p3, arethmetic_and_logic_unit_1_sum, data_ram_1_p6, multiplexer_1_out,
       multiplexer_2_out, multiplexer_4_out, multiplexer_5_out, PC_plus_4, program_counter_1_instr_addr,
       register_file_1_p4, register_file_1_p7, register_file_1_p8, shifter_1_p2, Sign_extender_2_p2,
       Sign_extender_3_p2;
  wire [31:1] large_sign_extender_1_p1, Sign_extender_p1;
  wire [31:31] large_sign_extender_1_p1_2, Sign_extender_p1_2;

  Multiplexer #(.Bits(32)) multiplexer_1 (
    .sel(arethmetic_and_logic_unit_1_bcond), .in_0(PC_plus_4), .in_1(adder_2_p1), .out(multiplexer_1_out));
  Multiplexer #(.Selector_Bits(2), .Bits(32)) multiplexer_2 (
    .sel(PC_mux), .in_0({arethmetic_and_logic_unit_1_sum[31:1], 1'b0}), .in_1(adder_2_p1), .in_2(PC_plus_4),
    .in_3(multiplexer_1_out), .out(multiplexer_2_out));
  // Probe on PC_plus_4
  // Probe on adder_2_p1
  // Probe on {arethmetic_and_logic_unit_1_sum[31:1], 1'b0}
  program_counter program_counter_1 (
    .instr_addr(program_counter_1_instr_addr), .clock(clk), .write(1'b1), .new_addr(multiplexer_2_out));
  // Probe on multiplexer_2_out
  // adder adder_1: pin names not known; wires that end beside it: PC_plus_4, program_counter_1_instr_addr, 32'h4
  // adder adder_2: pin names not known; wires that end beside it: adder_2_p1, program_counter_1_instr_addr, adder_2_p3
  // Probe on program_counter_1_instr_addr
  // Probe on {Sign_extender_p1, 1'b0}
  Multiplexer #(.Bits(32)) multiplexer_3 (
    .sel(SUM_mux), .in_0({large_sign_extender_1_p1, 1'b0}), .in_1({Sign_extender_p1, 1'b0}), .out(adder_2_p3));
  // Probe on {large_sign_extender_1_p1, 1'b0}
  Instructions_rom instructions_rom_1 (
    .instr({_31, _30, _30_21, _20, imm_19_12, funct3_14_12, _11_8, _7, opcode_6_0[6], _5, opcode_6_0[4:0]}),
    .addr(program_counter_1_instr_addr));
  // Probe on {_31, _30, _30_21, _20, imm_19_12, funct3_14_12, _11_8, _7, opcode_6_0[6], _5, opcode_6_0[4:0]}
  // sign_extender Sign_extender: pin names not known; wires that end beside it: {Sign_extender_p1_2[31], Sign_extender_p1}, {_31, _7, _30, _30_21[8:4], _11_8}
  // large_sign_extender large_sign_extender_1: pin names not known; wires that end beside it: {large_sign_extender_1_p1_2[31], large_sign_extender_1_p1}, {_31, imm_19_12, funct3_14_12, _20, _30, _30_21}
  control_unit control_unit_1 (
    .PC_mux(PC_mux), .RF_w(RF_w), .A_mux(A_mux), .B_mux(B_mux), .ALU_mux(ALU_mux), .RAM_w(RAM_w),
    .RF_mux(RF_mux), .SUM_mux(SUM_mux), .instr({opcode_6_0[6], _5, opcode_6_0[4:2]}));
  // Probe on {_11_8, _7}
  // register_file register_file_1: pin names not known; wires that end beside it: imm_19_12, {_30_21[3:0], _20}, {_11_8, _7}, register_file_1_p4, clk, RF_w, register_file_1_p7, register_file_1_p8
  // Probe on imm_19_12
  // Probe on {_30_21[3:0], _20}
  // sign_extender Sign_extender_2: pin names not known; wires that end beside it: {_31, _30, _30_21, _20}, Sign_extender_2_p2
  // sign_extender Sign_extender_3: pin names not known; wires that end beside it: {_31, _30, _30_21[8:4], _11_8, _7}, Sign_extender_3_p2
  // shifter shifter_1: pin names not known; wires that end beside it: {_31, _30, _30_21, _20, imm_19_12, funct3_14_12}, shifter_1_p2
  // Probe on register_file_1_p7
  // Probe on register_file_1_p8
  // Probe on Sign_extender_2_p2
  // Probe on Sign_extender_3_p2
  // Probe on register_file_1_p4
  // Probe on shifter_1_p2
  Multiplexer #(.Bits(32)) multiplexer_4 (
    .sel(A_mux), .in_0(program_counter_1_instr_addr), .in_1(register_file_1_p7), .out(multiplexer_4_out));
  Multiplexer #(.Selector_Bits(2), .Bits(32)) multiplexer_5 (
    .sel(B_mux), .in_0(register_file_1_p8), .in_1(Sign_extender_2_p2), .in_2(Sign_extender_3_p2),
    .in_3(shifter_1_p2), .out(multiplexer_5_out));
  arethmetic_and_logic_unit arethmetic_and_logic_unit_1 (
    .A(multiplexer_4_out), .B(multiplexer_5_out), .func(multiplexer_6_out), ._30(_30),
    .Sum(arethmetic_and_logic_unit_1_sum), .Bcond(arethmetic_and_logic_unit_1_bcond), ._5(_5));
  Multiplexer #(.Bits(3)) multiplexer_6 (.sel(ALU_mux), .in_0(funct3_14_12), .in_1(3'b000), .out(multiplexer_6_out));
  // Probe on funct3_14_12
  // Probe on arethmetic_and_logic_unit_1_sum
  // data_ram data_ram_1: pin names not known; wires that end beside it: arethmetic_and_logic_unit_1_sum, register_file_1_p8, clk, funct3_14_12, RAM_w, data_ram_1_p6
  Multiplexer #(.Selector_Bits(2), .Bits(32)) multiplexer_7 (
    .sel(RF_mux), .in_0(shifter_1_p2), .in_1(arethmetic_and_logic_unit_1_sum), .in_2(data_ram_1_p6),
    .in_3(PC_plus_4), .out(register_file_1_p4));
  // Probe on data_ram_1_p6

  // Other names for the same wires on the sheet: opcode_6_0[5] = _5; rd_11_7[4:0] = {_11_8, _7};
  //   imm_19_12[2:0] = funct3_14_12; imm_31_12[19:0] = {_31, _30, _30_21, _20, imm_19_12, funct3_14_12};
  //   rs1_19_15[4:0] = imm_19_12; imm_31_20[11:0] = {_31, _30, _30_21, _20}; rs2_24_20[4:0] = {_30_21[3:0], _20};
  //   _30_25[5:0] = {_30, _30_21[8:4]}; imm_31_25[6:0] = {_31, _30, _30_21[8:4]}; _30_21[9] = _30; clock = clk

  // Notes on the sheet:
  //   PC
  //   +
  //   ROM
  //   branch
  //   jal
  //   sign ext
  //   CU
  //   jalr
  //   RF
  //   upper imm
  //   imm
  //   store
  //   shifter
  //   ALU
  //   RAM
endmodule
