// Digital circuit program counter.dig as structural Verilog
module program_counter (
  input  clock,
  input  write,
  input  [31:0] new_addr,
  output [31:0] instr_addr
);

  CounterPreset #(.Bits(32)) counter (
    .en(1'b0), .C(clock), .dir(1'b0), .in(new_addr), .ld(write), .clr(1'b0), .out(instr_addr));  // open: ovf
endmodule
